// Logisim project 8 bit ALU.circ as structural Verilog
module ALU (
  input  [7:0] OPERAND_2,
  input  [7:0] OPERAND_1,
  input  CIN,
  input  CIN_2,
  input  [3:0] OPCODE,
  input  OE,
  output COUT,
  output COUT_2,
  output [7:0] OUTPUT,
  output out_10,
  output GT,
  output EQ,
  output LT
);

  wire [2:0] bit_extender_1_out, bit_extender_2_out;
  wire [7:0] adder_1_out, adder_2_out, and_1_out, multiplexer_1_out, not_1_out, or_1_out, shifter_1_out,
       shifter_2_out, subtractor_1_out;

  Bit_Extender #(.out_width(3)) bit_extender_1 (.in(OPERAND_2), .out(bit_extender_1_out));
  Bit_Extender #(.out_width(3)) bit_extender_2 (.in(OPERAND_2), .out(bit_extender_2_out));
  Adder adder_1 (.a(OPERAND_1), .b(OPERAND_2), .out(adder_1_out), .cin(CIN), .cout(COUT));
  Adder adder_2 (.a(OPERAND_1), .b(8'h1), .out(adder_2_out), .cin(CIN_2), .cout(COUT_2));
  Subtractor subtractor_1 (.a(OPERAND_1), .b(8'h1), .out(subtractor_1_out), .bout(out_10));  // open: bin
  Comparator comparator_1 (.a(OPERAND_1), .b(OPERAND_2), .gt(GT), .eq(EQ), .lt(LT));
  assign not_1_out = ~OPERAND_1;  // NOT_Gate not_1, 8 bits wide
  assign and_1_out = OPERAND_1 & OPERAND_2;  // AND_Gate and_1, 8 bits wide
  assign or_1_out = OPERAND_1 | OPERAND_2;  // OR_Gate or_1, 8 bits wide
  Shifter #(.shift("lr")) shifter_1 (.in(OPERAND_1), .\dist (bit_extender_1_out), .out(shifter_1_out));
  Shifter shifter_2 (.in(OPERAND_1), .\dist (bit_extender_2_out), .out(shifter_2_out));
  Multiplexer #(.select(4), .width(8)) multiplexer_1 (
    .in0(adder_1_out), .in1(adder_2_out), .in2(subtractor_1_out), .in3(not_1_out), .in4(and_1_out),
    .in5(or_1_out), .in6(shifter_1_out), .in7(shifter_2_out), .out(multiplexer_1_out), .sel(OPCODE), .en(OE));  // open: in8, in9, in10, in11, in12, in13, in14, in15
  assign OUTPUT = multiplexer_1_out;  // Buffer buffer_1, 8 bits wide
endmodule
